# Fritzing sketch diagram (saved by Fritzing 0.9.4)
breadboards: 1

parts:
  U1 = LCD-16X2 [package=lcd-16x2_noholes]
  R1 = TRIMPOT [package=3362u-2]
  Raspberry_Pi_1 = Raspberry Pi 3 [part_number=RPI-3-V1.2]
  元件2 = MQ-9 breakout

nets:
  GND: U1.VSS, U1.R_W, U1.K, R1.CCW, Raspberry_Pi_1.GND, 元件2.GND
  VDD: U1.VDD, U1.A, Raspberry_Pi_1.5V, 元件2.VCC
  N1: U1.VO, R1.WIPER
  N2: U1.RS, Raspberry_Pi_1.GPIO26
  N3: U1.E, Raspberry_Pi_1.GPIO19
  N4: U1.DB4, Raspberry_Pi_1.GPIO13
  N5: U1.DB5, Raspberry_Pi_1.GPIO6
  N6: U1.DB6, Raspberry_Pi_1.GPIO5
  N7: U1.DB7, Raspberry_Pi_1.GPIO11
  N8: Raspberry_Pi_1.GPIO9, 元件2.DO

custom parts:
  MQ-9 breakout: SKU: 101284
